# Fritzing sketch Sound Sensor (saved by Fritzing 0.9.3b)
breadboards: 1

parts:
  Mod1 = Raspberry Pi Pico
  Part1 = Breakout Board for Electret Microphone
  D1 = LED_BARGRAPH_10 [package=led_bargaph_10]
  R1 = Resistor [tolerance=±5% resistance=220 package=THT]
  R2 = Resistor [tolerance=±5% resistance=220 package=THT]
  R3 = Resistor [tolerance=±5% resistance=220 package=THT]
  R4 = Resistor [tolerance=±5% resistance=220 package=THT]
  R5 = Resistor [tolerance=±5% resistance=220 package=THT]
  R6 = Resistor [tolerance=±5% resistance=220 package=THT]
  R7 = Resistor [tolerance=±5% resistance=220 package=THT]
  R8 = Resistor [tolerance=±5% resistance=220 package=THT]
  R9 = Resistor [tolerance=±5% resistance=220 package=THT]
  R10 = Resistor [tolerance=±5% resistance=220 package=THT]

nets:
  N1: Mod1.pin_3, Mod1.pin_8, Mod1.pin_13, Mod1.pin_18, Mod1.pin_23, Mod1.pin_28, Mod1.pin_33, Mod1.pin_38, Mod1.pin_42, Part1.GND, R1.Pin_0, R2.Pin_0, R3.Pin_0, R4.Pin_0, R5.Pin_0, R6.Pin_0, R7.Pin_0, R8.Pin_0, R9.Pin_0, R10.Pin_0
  N2: Mod1.pin_6, D1.J_A
  N3: Mod1.pin_21, D1.I_A
  N4: Mod1.pin_22, D1.H_A
  N5: Mod1.pin_24, D1.G_A
  N6: Mod1.pin_25, D1.F_A
  N7: Mod1.pin_26, D1.E_A
  N8: Mod1.pin_27, D1.D_A
  N9: Mod1.pin_29, D1.C_A
  N10: Mod1.pin_31, Part1.AUD
  N11: Mod1.pin_32, D1.B_A
  N12: Mod1.pin_34, D1.A_A
  N13: Mod1.pin_40, Part1.VCC
  N14: D1.J_C, R9.Pin_1
  N15: D1.I_C, R8.Pin_1
  N16: D1.H_C, R7.Pin_1
  N17: D1.G_C, R6.Pin_1
  N18: D1.F_C, R10.Pin_1
  N19: D1.E_C, R5.Pin_1
  N20: D1.D_C, R4.Pin_1
  N21: D1.C_C, R3.Pin_1
  N22: D1.B_C, R2.Pin_1
  N23: D1.A_C, R1.Pin_1

custom parts:
  Raspberry Pi Pico: Raspberry Pi Pico. Based around the RP2040 microcontroller the Pico is a low cost microcontroller device bringing Raspberry Pi quality, cost, and easy of use to the microcontroller space. Jan 2021, Split part in to two versions: tht (this one) and SMD. This one will drill holes for a .1 in header in pcb to allow plugging in the module as well as providing pads to solder the module to the top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
