# Fritzing sketch test_1 (saved by Fritzing 0.9.3b)
breadboards: 1

parts:
  Mod1 = Raspberry Pi Pico
  S1 = Pushbutton [package="[THT]"]
  S2 = Pushbutton [package="[THT]"]
  S3 = Pushbutton [package="[THT]"]
  S4 = Pushbutton [package="[THT]"]
  R_Button_Cancel = Resistor [tolerance=±5% resistance=10k package=THT]
  R_Button_Up = Resistor [tolerance=±5% resistance=10k package=THT]
  R_Button_Down = Resistor [tolerance=±5% resistance=10k package=THT]
  R_Button_Enter = Resistor [tolerance=±5% resistance=10k package=THT]
  RHT1 = Humidity and Temperature Sensor RHT03
  R_DHT22 = Resistor [tolerance=±5% resistance=10k package=THT]
  Squix1 = OLED 0.96" 128x64 I2C SSD1306

nets:
  N1: Mod1.pin_1, S1.Pin_3, S1.Pin_4, R_Button_Cancel.Pin_0
  N2: Mod1.pin_2, S2.Pin_3, S2.Pin_4, R_Button_Up.Pin_0
  N3: Mod1.pin_3, Mod1.pin_8, Mod1.pin_13, Mod1.pin_18, Mod1.pin_23, Mod1.pin_28, Mod1.pin_33, Mod1.pin_38, Mod1.pin_42, R_Button_Cancel.Pin_1, R_Button_Up.Pin_1, R_Button_Down.Pin_1, R_Button_Enter.Pin_1, RHT1.GND_2, Squix1.GND
  VCC: Mod1.pin_4, Mod1.pin_36, S1.Pin_1, S1.Pin_2, S2.Pin_1, S2.Pin_2, S3.Pin_1, S3.Pin_2, S4.Pin_1, S4.Pin_2, RHT1.Vcc, R_DHT22.Pin_0, Squix1.VCC
  N4: Mod1.pin_5, S4.Pin_3, S4.Pin_4, R_Button_Enter.Pin_0
  N5: Mod1.pin_17, RHT1.Data-signal, R_DHT22.Pin_1
  N6: Mod1.pin_19, Squix1.SCA
  N7: Mod1.pin_20, Squix1.SCL
  N8: S3.Pin_3, S3.Pin_4, R_Button_Down.Pin_0

custom parts:
  Raspberry Pi Pico: Raspberry Pi Pico. Based around the RP2040 microcontroller the Pico is a low cost microcontroller device bringing Raspberry Pi quality, cost, and easy of use to the microcontroller space. Jan 2021, Split part in to two versions: tht (this one) and SMD. This one will drill holes for a .1 in header in pcb to allow plugging in the module as well as providing pads to solder the module to the top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
